# Fritzing sketch ESQUEMATICO2 (saved by Fritzing 0.9.3b)
breadboards: 1

parts:
  Componente1 = FTDI Basic Programmer
  Mod1 = ESP32 - CAM

nets:
  N1: Componente1.RXI, Mod1.VOT
  N2: Componente1.TXO, Mod1.VOR
  GND: Componente1.GND, Mod1.GND, Mod1.IO0

custom parts:
  ESP32 - CAM: The ESP32-CAM has a very competitive small-size camera module that can operate independently as a minimum system with a footprint of only 27*40.5*4.5mm and a deep sleep current of up to 6mA.
