# Fritzing sketch ESQUEMATICO3 (saved by Fritzing 0.9.3b)
breadboards: 1

parts:
  Componente1 = FTDI Basic Programmer
  Mod1 = ESP32 - CAM
  M1 = DC Motor
  S1 = H-Bridge with L298N
  M2 = DC Motor

nets:
  N1: Componente1.RXI, Mod1.VOT
  N2: Componente1.TXO, Mod1.VOR
  GND: Componente1.GND, Mod1.GND, S1.GND
  N3: Mod1.IO12, S1.IN3
  N4: Mod1.IO13, S1.IN4
  N5: Mod1.IO15, S1.IN1
  N6: Mod1.IO14, S1.IN2
  N7: M1.pin_1, S1.M2-02
  N8: M1.pin_2, S1.M2-01
  N9: S1.ENA, S1.ENA-5V
  N10: S1.ENB, S1.ENB-5V
  N11: S1.M1-01, M2.pin_2
  N12: S1.M1-02, M2.pin_1

custom parts:
  ESP32 - CAM: The ESP32-CAM has a very competitive small-size camera module that can operate independently as a minimum system with a footprint of only 27*40.5*4.5mm and a deep sleep current of up to 6mA.
  H-Bridge with L298N: h-bridge
