# Fritzing sketch ESQUEMATICO4 (saved by Fritzing 0.9.3b)
breadboards: 1

parts:
  Componente1 = FTDI Basic Programmer
  Mod1 = ESP32 - CAM
  M1 = DC Motor
  S1 = H-Bridge with L298N
  HC-SR04_Sensor_1 = HC-SR04 Ultrasonic Distance Sensor
  M2 = DC Motor

nets:
  N1: Componente1.RXI, Mod1.VOT
  N2: Componente1.TXO, Mod1.VOR
  GND: Componente1.GND, Mod1.GND, S1.GND, HC-SR04_Sensor_1.GND
  5V: Mod1.5V, HC-SR04_Sensor_1.VCC
  N3: Mod1.IO12, S1.IN3
  N4: Mod1.IO13, S1.IN4
  N5: Mod1.IO15, S1.IN1
  N6: Mod1.IO14, S1.IN2
  N7: Mod1.IO2, HC-SR04_Sensor_1.TRIG
  N8: Mod1.IO4, HC-SR04_Sensor_1.ECHO
  N9: M1.pin_1, S1.M2-02
  N10: M1.pin_2, S1.M2-01
  N11: S1.ENA, S1.ENA-5V
  N12: S1.ENB, S1.ENB-5V
  N13: S1.M1-01, M2.pin_2
  N14: S1.M1-02, M2.pin_1

custom parts:
  ESP32 - CAM: The ESP32-CAM has a very competitive small-size camera module that can operate independently as a minimum system with a footprint of only 27*40.5*4.5mm and a deep sleep current of up to 6mA.
  H-Bridge with L298N: h-bridge

// code stored in the sketch: Sensor_Ultrasonido-hc_sr04.ino
long distancia;
long tiempo;
void setup(){
  Serial.begin(9600);
  pinMode(IO04, OUTPUT); /activación del pin 4 como salida: para el pulso ultrasónico/
  pinMode(IO02, INPUT); /activación del pin 2 como entrada: tiempo del rebote del ultrasonido/
}

void loop(){
  digitalWrite(4,LOW); /* Por cuestión de estabilización del sensor*/
  delayMicroseconds(5);
  digitalWrite(2, HIGH); /* envío del pulso ultrasónico*/
  delayMicroseconds(10);
  tiempo=pulseIn(2, HIGH); /* Función para medir la longitud del pulso entrante. Mide el tiempo que transcurrido entre el envío
  del pulso ultrasónico y cuando el sensor recibe el rebote, es decir: desde que el pin 12 empieza a recibir el rebote, HIGH, hasta que
  deja de hacerlo, LOW, la longitud del pulso entrante*/
  distancia= int(0.017*tiempo); /fórmula para calcular la distancia obteniendo un valor entero/
  /Monitorización en centímetros por el monitor serial/
  Serial.println("Distancia ");
  Serial.println(distancia);
  Serial.println(" cm");
  delay(1000);
}
