# Fritzing sketch ESQUEMATICO1_PROTOTIPO-ILUINAL (saved by Fritzing 0.9.3b)
breadboards: 1

parts:
  Sensore_PIR_HC-SR502 = HC-SR501 Body Sensor Module
  KY-1 = Keyes Relay [package=THT]
  M1 = RioRand LM2596
  Componente2 = node32s
  SIM800L_BO1 = SIM800L BO
  Part2 = Solar Cell
  R1 = Photocell (LDR) [package=THT]  # not connected
  LED2 = LEDs [package=led10mm]
  R2 = Resistor [tolerance=±5% resistance=220 package=THT]
  Bat6 = battery_holder_single_18650
  Bat7 = battery_holder_single_18650
  TP1 = TP4056 [chip_label=TP4056 package="DIP (Dual Inline) [THT]"]
  D1 = Diode [package=diode-1n4001]

nets:
  N1: Sensore_PIR_HC-SR502.VCC, KY-1.signal, M1.Pin_3, Componente2.V_BATT, SIM800L_BO1.PIN2
  N2: Sensore_PIR_HC-SR502.OUT, Componente2.IO14
  GND: Sensore_PIR_HC-SR502.GND, KY-1.ground, M1.Pin_4, Componente2.GND, SIM800L_BO1.pin_6
  N3: KY-1.power, Componente2.IO25
  N4: KY-1.NC, KY-1.C, KY-1.NO, Bat6.+#0, TP1.pin4
  N5: M1.Pin_1, TP1.pin3
  N6: M1.Pin_2, TP1.pin6
  N7: Componente2.IO4, SIM800L_BO1.pin_4
  N8: Componente2.IO0, SIM800L_BO1.pin_5
  N9: Part2.+, D1.C
  N10: Part2.-, TP1.pin2
  N11: LED2.C, Bat7.+#1, TP1.pin5
  N12: LED2.A, R2.Pin_1
  N13: Bat6.+#1, Bat7.+#0

custom parts:
  HC-SR501 Body Sensor Module: Pyroelectric Infrared PIR Motion Sensor Detector Module
  Keyes Relay: The Keyes 5V relay module is suitable for SCM development, home appliance control. It uses a 5V~12V TIL control signal which can control DC / AC signal.
  battery_holder_single_18650: single 18650 battery holder
  TP4056: A DIP stand-in part for whatever IC you want. With 6 pins on a 300mil dual inline package (DIP) footprint.

// code stored in the sketch: Sensor_Ultrasonido-hc_sr04.ino
// SENSOR ULTRASONIDO hc-sr04

long distancia;
long tiempo;
void setup(){
  Serial.begin(9600);
  pinMode(IO04, OUTPUT); /activación del pin 4 como salida: para el pulso ultrasónico/
  pinMode(IO02, INPUT); /activación del pin 2 como entrada: tiempo del rebote del ultrasonido/
}

void loop(){
  digitalWrite(4,LOW); /* Por cuestión de estabilización del sensor*/
  delayMicroseconds(5);
  digitalWrite(2, HIGH); /* envío del pulso ultrasónico*/
  delayMicroseconds(10);
  tiempo=pulseIn(2, HIGH); /* Función para medir la longitud del pulso entrante. Mide el tiempo que transcurrido entre el envío
  del pulso ultrasónico y cuando el sensor recibe el rebote, es decir: desde que el pin 12 empieza a recibir el rebote, HIGH, hasta que
  deja de hacerlo, LOW, la longitud del pulso entrante*/
  distancia= int(0.017*tiempo); /fórmula para calcular la distancia obteniendo un valor entero/
  /Monitorización en centímetros por el monitor serial/
  Serial.println("Distancia ");
  Serial.println(distancia);
  Serial.println(" cm");
  delay(1000);
}

// BLINK ESP32
int led = 2; // PIN GPIO 02 LED EN PLACA DEVKIT ESP32


void setup() {
  // put your setup code here, to run once:


Serial.begin(115200);
pinMode(led, OUTPUT);


}


void loop() {
  // put your main code here, to run repeatedly:


digitalWrite(led, HIGH);
Serial.println("LED ACTIVADO");
delay(1000);
digitalWrite(led, LOW);
Serial.println("LED DESACTIVADO");
delay(1000);
}
