# Fritzing sketch proyecto_imposible_SMS (saved by Fritzing 0.9.3b)
breadboards: 1

parts:
  Componente2 = Arduino Ethernet Shield (Rev3)
  e-radionica_com1 = LM393 LDR breakout [part_number=100027]
  PIR1 = PIR sensor
  SIM800L_BO1 = SIM800L BO
  U1 = LM2596 step down module
  KY-1 = Keyes Relay [package=THT]
  VCC1 = Battery
  USBTTL1 = USB TTL Serial Cable
  LED1 = LEDs [package=led10mm]

nets:
  N1: Componente2.ETH_CS, SIM800L_BO1.pin_4
  N2: Componente2.PWM_D11, SIM800L_BO1.pin_5
  N3: Componente2.SPI/D12, KY-1.signal
  N4: Componente2.D2, e-radionica_com1.DO
  N5: Componente2.SDCS, PIR1.SIG
  5V: Componente2.5V, e-radionica_com1.VCC, PIR1.VDD, KY-1.power
  GND: Componente2.GND, e-radionica_com1.GND, PIR1.GND, KY-1.ground
  N6: SIM800L_BO1.PIN2, SIM800L_BO1.PIN3, U1.OUT+
  N7: SIM800L_BO1.pin_6, U1.OUT-
  N8: KY-1.NC, LED1.C
  N9: KY-1.C, LED1.A
  N10: VCC1.-, USBTTL1.GND

custom parts:
  LM2596 step down module: LM2596 DC-DC step down power supply module 3 A.
  Keyes Relay: The Keyes 5V relay module is suitable for SCM development, home appliance control. It uses a 5V~12V TIL control signal which can control DC / AC signal.
  Battery: Your standard 2x 18650 battery pack (7,4 Volts)
